// Logisim project decodificador.circ as structural Verilog: 4 circuits, main circuit main
module main (
  input  A3,
  input  A2,
  input  cargar_inicio,
  input  A1,
  input  A0
);

  wire clock_1_out, d_ff_1_q, d_ff_2_q, d_ff_3_q, d_ff_4_q, decodificador_display_1_a,
       decodificador_display_1_b, decodificador_display_1_c, decodificador_display_1_d,
       decodificador_display_1_e, decodificador_display_1_f, decodificador_display_1_g,
       decodificador_entrada_1_nodoa, decodificador_entrada_1_nodob, decodificador_entrada_1_nodoc,
       decodificador_entrada_1_nodod, decodificador_entrada_1_nodoe, decodificador_entrada_1_nodof,
       decodificador_entrada_1_nodog, decodificador_entrada_1_nodoh, decodificador_entrada_1_nodoi,
       decodificador_entrada_1_nodoj, decodificador_entrada_1_nodok, decodificador_entrada_1_nodol,
       decodificador_entrada_1_nodom, decodificador_entrada_1_nodon, decodificador_entrada_1_nodoo,
       decodificador_entrada_1_nodop, logica_transicion_1_n0, logica_transicion_1_n1, logica_transicion_1_n2,
       logica_transicion_1_n3, multiplexer_1_out, multiplexer_2_out, multiplexer_3_out, multiplexer_4_out;

  Multiplexer multiplexer_1 (.in0(logica_transicion_1_n3), .in1(A3), .out(multiplexer_1_out), .sel(cargar_inicio));
  Multiplexer multiplexer_2 (.in0(logica_transicion_1_n2), .in1(A2), .out(multiplexer_2_out), .sel(cargar_inicio));
  Multiplexer multiplexer_3 (.in0(logica_transicion_1_n1), .in1(A1), .out(multiplexer_3_out), .sel(cargar_inicio));
  Multiplexer multiplexer_4 (.in0(logica_transicion_1_n0), .in1(A0), .out(multiplexer_4_out), .sel(cargar_inicio));
  Clock clock_1 (.out(clock_1_out));
  D_Flip_Flop d_ff_1 (.D(multiplexer_1_out), .clk(clock_1_out), .Q(d_ff_1_q));  // open: Qn, preset, reset
  D_Flip_Flop d_ff_2 (.D(multiplexer_2_out), .clk(clock_1_out), .Q(d_ff_2_q));  // open: Qn, preset, reset
  D_Flip_Flop d_ff_3 (.D(multiplexer_3_out), .clk(clock_1_out), .Q(d_ff_3_q));  // open: Qn, preset, reset
  D_Flip_Flop d_ff_4 (.D(multiplexer_4_out), .clk(clock_1_out), .Q(d_ff_4_q));  // open: Qn, preset, reset
  decodificador_entrada decodificador_entrada_1 (
    .A3(A3), .A2(A2), .A1(A1), .A0(A0), .NodoA(decodificador_entrada_1_nodoa),
    .NodoB(decodificador_entrada_1_nodob), .NodoC(decodificador_entrada_1_nodoc),
    .NodoD(decodificador_entrada_1_nodod), .NodoE(decodificador_entrada_1_nodoe),
    .NodoF(decodificador_entrada_1_nodof), .NodoG(decodificador_entrada_1_nodog),
    .NodoH(decodificador_entrada_1_nodoh), .NodoI(decodificador_entrada_1_nodoi),
    .NodoJ(decodificador_entrada_1_nodoj), .NodoK(decodificador_entrada_1_nodok),
    .NodoL(decodificador_entrada_1_nodol), .NodoM(decodificador_entrada_1_nodom),
    .NodoN(decodificador_entrada_1_nodon), .NodoO(decodificador_entrada_1_nodoo),
    .NodoP(decodificador_entrada_1_nodop));
  LED led_1 (.in(decodificador_entrada_1_nodoa));
  LED led_2 (.in(decodificador_entrada_1_nodob));
  LED led_3 (.in(decodificador_entrada_1_nodoc));
  LED led_4 (.in(decodificador_entrada_1_nodod));
  LED led_5 (.in(decodificador_entrada_1_nodoe));
  LED led_6 (.in(decodificador_entrada_1_nodof));
  LED led_7 (.in(decodificador_entrada_1_nodog));
  LED led_8 (.in(decodificador_entrada_1_nodoh));
  LED led_9 (.in(decodificador_entrada_1_nodoi));
  LED led_10 (.in(decodificador_entrada_1_nodoj));
  LED led_11 (.in(decodificador_entrada_1_nodok));
  LED led_12 (.in(decodificador_entrada_1_nodol));
  LED led_13 (.in(decodificador_entrada_1_nodom));
  LED led_14 (.in(decodificador_entrada_1_nodon));
  LED led_15 (.in(decodificador_entrada_1_nodoo));
  LED led_16 (.in(decodificador_entrada_1_nodop));
  logica_transicion logica_transicion_1 (
    .S3(d_ff_1_q), .S2(d_ff_2_q), .S1(d_ff_3_q), .S0(d_ff_4_q), .N3(logica_transicion_1_n3),
    .N2(logica_transicion_1_n2), .N1(logica_transicion_1_n1), .N0(logica_transicion_1_n0));
  decodificador_display decodificador_display_1 (
    .N3(d_ff_1_q), .N2(d_ff_2_q), .N1(d_ff_3_q), .N0(d_ff_4_q), .a(decodificador_display_1_a),
    .b(decodificador_display_1_b), .c(decodificador_display_1_c), .d(decodificador_display_1_d),
    .e(decodificador_display_1_e), .f(decodificador_display_1_f), .g(decodificador_display_1_g));
  _7_Segment_Display u_7_segment_display_1 (
    .g(decodificador_display_1_g), .f(decodificador_display_1_f), .a(decodificador_display_1_a),
    .b(decodificador_display_1_b), .e(decodificador_display_1_e), .d(decodificador_display_1_d),
    .c(decodificador_display_1_c));  // open: dp
endmodule

module decodificador_entrada (
  input  A3,
  input  A2,
  input  A1,
  input  A0,
  output NodoA,
  output NodoB,
  output NodoC,
  output NodoD,
  output NodoE,
  output NodoF,
  output NodoG,
  output NodoH,
  output NodoI,
  output NodoJ,
  output NodoK,
  output NodoL,
  output NodoM,
  output NodoN,
  output NodoO,
  output NodoP
);

  wire and_15_out, and_16_out, and_17_out, and_18_out, and_19_out, not_1_out, not_2_out, not_3_out, not_4_out;

  not not_1 (not_1_out, A3);
  not not_2 (not_2_out, A2);
  not not_3 (not_3_out, A1);
  not not_4 (not_4_out, A0);
  and and_1 (NodoA, not_1_out, not_2_out, not_3_out, not_4_out);
  and and_2 (NodoB, not_1_out, not_2_out, not_3_out, A0);
  and and_3 (NodoC, not_1_out, not_2_out, A1, not_4_out);
  and and_4 (NodoD, not_1_out, not_2_out, A1, A0);
  and and_5 (NodoE, not_1_out, A2, not_3_out, not_4_out);
  and and_6 (NodoF, not_1_out, A2, not_3_out, A0);
  and and_7 (NodoG, not_1_out, A2, A1, not_4_out);
  and and_8 (NodoH, not_1_out, A2, A1, A0);
  and and_9 (NodoI, A3, not_2_out, not_3_out, not_4_out);
  and and_10 (NodoJ, A3, not_2_out, not_3_out, A0);
  and and_11 (NodoK, A3, not_2_out, A1, not_4_out);
  and and_12 (NodoL, A3, not_2_out, A1, A0);
  and and_13 (NodoM, A3, A2, not_3_out, not_4_out);
  and and_14 (NodoN, A3, A2, not_3_out, A0);
  and and_15 (and_15_out, not_1_out, not_2_out, not_3_out, A0);
  and and_16 (and_16_out, not_1_out, not_2_out, A1, not_4_out);
  and and_17 (and_17_out, A3, A2, A1, not_4_out);
  and and_18 (and_18_out, not_1_out, not_2_out, not_3_out, A0);
  and and_19 (and_19_out, A3, A2, A1, A0);
  or or_1 (NodoO, and_15_out, and_16_out, and_17_out);
  or or_2 (NodoP, and_18_out, and_19_out);
endmodule

module decodificador_display (
  input  N3,
  input  N2,
  input  N1,
  input  N0,
  output a,
  output b,
  output c,
  output d,
  output e,
  output f,
  output g
);

  wire and_1_out, and_2_out, and_3_out, and_4_out, and_5_out, and_6_out, and_7_out, and_8_out, and_9_out,
       and_10_out, and_11_out, and_12_out, and_13_out, and_14_out, and_15_out, and_16_out, and_17_out,
       and_18_out, and_19_out, and_20_out, and_21_out, and_22_out, and_23_out, and_24_out, and_25_out,
       and_26_out, and_27_out, and_28_out, and_29_out, and_30_out, and_31_out, not_1_out, not_2_out,
       not_3_out, not_4_out;

  not not_1 (not_1_out, N3);
  not not_2 (not_2_out, N2);
  not not_3 (not_3_out, N1);
  not not_4 (not_4_out, N0);
  and and_1 (and_1_out, not_1_out, not_2_out, not_4_out);
  and and_2 (and_2_out, N2, N0);
  and and_3 (and_3_out, N3, N0);
  and and_4 (and_4_out, N2, N1);
  and and_5 (and_5_out, not_1_out, N1);
  and and_6 (and_6_out, not_3_out, not_4_out);
  and and_7 (and_7_out, not_1_out, N2, not_3_out);
  and and_8 (and_8_out, N2, not_4_out);
  and and_9 (and_9_out, N3, not_2_out, N0);
  and and_10 (and_10_out, N1, not_4_out);
  and and_11 (and_11_out, not_1_out, not_2_out, N0);
  and and_12 (and_12_out, N3, not_3_out);
  and and_13 (and_13_out, not_1_out, not_2_out, not_4_out);
  and and_14 (and_14_out, not_2_out, N1);
  and and_15 (and_15_out, not_1_out, N2, not_3_out, N0);
  and and_16 (and_16_out, N1, not_4_out);
  and and_17 (and_17_out, N3, N2, not_4_out);
  and and_18 (and_18_out, N3, N1);
  and and_19 (and_19_out, N1, N0);
  and and_20 (and_20_out, N3, N0);
  and and_21 (and_21_out, not_1_out, N2, not_4_out);
  and and_22 (and_22_out, N3, not_2_out);
  and and_23 (and_23_out, not_1_out, not_3_out, not_4_out);
  and and_24 (and_24_out, not_1_out, N0);
  and and_25 (and_25_out, not_2_out, N1);
  and and_26 (and_26_out, N2, not_3_out);
  and and_27 (and_27_out, N3, not_4_out);
  and and_28 (and_28_out, not_2_out, not_4_out);
  and and_29 (and_29_out, N3, N1);
  and and_30 (and_30_out, not_1_out, N2, not_3_out);
  and and_31 (and_31_out, N3, N0);
  or or_1 (a, and_1_out, and_2_out, and_3_out, and_4_out, and_5_out);
  or or_2 (b, and_6_out, and_7_out, and_8_out, and_9_out);
  or or_3 (c, and_10_out, and_11_out, and_12_out);
  or or_4 (d, and_13_out, and_14_out, and_15_out, and_16_out, and_17_out, and_18_out);
  or or_5 (e, and_19_out, and_20_out, and_21_out, and_22_out, and_23_out);
  or or_6 (f, and_24_out, and_25_out, and_26_out, and_27_out);
  or or_7 (g, and_28_out, and_29_out, and_30_out, and_31_out);
endmodule

module logica_transicion (
  input  S3,
  input  S2,
  input  S1,
  input  S0,
  output N3,
  output N2,
  output N1,
  output N0
);

  wire and_1_out, and_2_out, and_3_out, and_4_out, and_5_out, and_6_out, and_7_out, and_8_out, and_9_out,
       and_10_out, and_11_out, and_12_out, and_13_out, and_14_out, and_15_out, and_16_out, not_1_out,
       not_2_out, not_3_out, not_4_out;

  not not_1 (not_1_out, S3);
  not not_2 (not_2_out, S2);
  not not_3 (not_3_out, S1);
  not not_4 (not_4_out, S0);
  and and_1 (and_1_out, not_1_out, S1, S0);
  and and_2 (and_2_out, S3, not_2_out);
  and and_3 (and_3_out, S3, not_3_out);
  and and_4 (and_4_out, S2, S0);
  and and_5 (and_5_out, S2, S1);
  and and_6 (and_6_out, S3, S0);
  and and_7 (and_7_out, S3, S1);
  and and_8 (and_8_out, S3, S2);
  and and_9 (and_9_out, not_1_out, not_2_out, not_3_out, S0);
  and and_10 (and_10_out, not_1_out, S2, not_4_out);
  and and_11 (and_11_out, S3, S2, not_3_out);
  and and_12 (and_12_out, not_1_out, not_3_out);
  and and_13 (and_13_out, not_2_out, not_4_out);
  and and_14 (and_14_out, S3, S1);
  and and_15 (and_15_out, S1, not_4_out);
  and and_16 (and_16_out, S3, S2, S0);
  or or_1 (N3, and_1_out, and_2_out, and_3_out);
  or or_2 (N2, and_4_out, and_5_out, and_6_out, and_7_out, and_8_out);
  or or_3 (N1, and_9_out, and_10_out, and_11_out);
  or or_4 (N0, and_12_out, and_13_out, and_14_out, and_15_out, and_16_out);
endmodule
